# Fritzing sketch Joybox Arduino (saved by Fritzing 0.6.3b)
breadboards: 1

parts:
  DIN1 = DIN-5 jack (MIDI) [package=THT]
  R1 = Resistor [resistance=220 tolerance=±5% package=THT]
  R2 = Resistor [tolerance=±5% resistance=220 package=THT]
  Part1 = Parallax_2_Axis_Joystick
  S1 = Pushbutton [package="[THT]"]
  R3 = Resistor [tolerance=±5% resistance=10k package=THT]
  Arduino2 = Arduino

nets:
  N1: DIN1.5, R2.Pin_0
  N2: DIN1.2, Part1.connector7, Part1.connector9, R3.Pin_0, Arduino2.GND, Arduino2.A2
  N3: DIN1.4, R1.Pin_0
  N4: R1.Pin_1, Part1.connector2, Part1.connector3, S1.Pin_1, S1.Pin_2, Arduino2.+5V
  N5: R2.Pin_1, Arduino2.D1TX
  N6: Part1.connector5, Arduino2.A3
  N7: S1.Pin_3, S1.Pin_4, R3.Pin_1, Arduino2.D11, Arduino2.D3

notes:
  JoyBoxMIDI
  By: TvHeadedRobots
  This is a joystick MIDI controller with a button. It is meant to be an open MIDI vrontroller platfomr that can easily be modified to do any possilbe control scheme that you can comeup with using an analog joystick and a button.
